# Fritzing sketch Diagram (saved by Fritzing 0.9.3b)

parts:
  Part1 = Arduino Uno (Rev3)
  Raystar_-_OLED = LCD screen [part_number=" REC001602EBPP5N00000"]
  J1 = double row male pin header, 4 pins [form="♂ (male)"]  # not connected
  Front_Panel_Connector = male pin header, 5 pins [form="♂ (male)"]

nets:
  N1: Part1.A5/SCL, Front_Panel_Connector.pin2
  N2: Part1.D8, Raystar_-_OLED.RS
  N3: Part1.D9_PWM, Raystar_-_OLED.V0
  N4: Part1.D10_PWM/SS, Raystar_-_OLED.VDD
  N5: Part1.D11_PWM/MOSI, Raystar_-_OLED.VSS
  N6: Part1.D2, Raystar_-_OLED.DB4
  N7: Part1.D4, Raystar_-_OLED.DB2
  N8: Part1.5V, Raystar_-_OLED.DB6
  N9: Part1.GND, Raystar_-_OLED.DB7

notes:
  Connected through USB for power and serial communication
  Use pin HDD- (Not HDD+)
  In the arduino enable the internal pullup resistor.
